// Logisim project Circuit.circ as structural Verilog: 4 circuits, main circuit regFile
module regFile (
  input  [31:0] INPUT_X,
  input  [3:0] inputADDRESSY,
  input  [3:0] inputADDRESSZ,
  input  [3:0] INPUTaddress,
  input  CLK,
  input  regW,
  output [31:0] outY,
  output [31:0] outZ
);

  wire and_1_out, decoder_1_out1, decoder_1_out2, decoder_1_out3, decoder_1_out4, decoder_1_out5,
       decoder_1_out6, decoder_1_out7, decoder_1_out8, decoder_1_out9, decoder_1_out10, decoder_1_out11,
       decoder_1_out12, decoder_1_out13, decoder_1_out14, decoder_1_out15;
  wire [31:0] R1, R2, R3, R4, R5, R6, R7, R8, R9, R10, R11, R12, R13, R14, R15;

  Decoder #(.select(4), .enable("false")) decoder_1 (
    .out1(decoder_1_out1), .out2(decoder_1_out2), .out3(decoder_1_out3), .out4(decoder_1_out4),
    .out5(decoder_1_out5), .out6(decoder_1_out6), .out7(decoder_1_out7), .out8(decoder_1_out8),
    .out9(decoder_1_out9), .out10(decoder_1_out10), .out11(decoder_1_out11), .out12(decoder_1_out12),
    .out13(decoder_1_out13), .out14(decoder_1_out14), .out15(decoder_1_out15), .sel(INPUTaddress));  // open: out0
  and and_1 (and_1_out, CLK, regW);
  Register #(.width(32)) register_1 (.D(INPUT_X), .en(decoder_1_out1), .Q(R1), .clk(and_1_out));  // open: clr
  Register #(.width(32)) register_2 (.D(INPUT_X), .en(decoder_1_out2), .Q(R2), .clk(and_1_out));  // open: clr
  Register #(.width(32)) register_3 (.D(INPUT_X), .en(decoder_1_out3), .Q(R3), .clk(and_1_out));  // open: clr
  Register #(.width(32)) register_4 (.D(INPUT_X), .en(decoder_1_out4), .Q(R4), .clk(and_1_out));  // open: clr
  Register #(.width(32)) register_5 (.D(INPUT_X), .en(decoder_1_out5), .Q(R5), .clk(and_1_out));  // open: clr
  Register #(.width(32)) register_6 (.D(INPUT_X), .en(decoder_1_out6), .Q(R6), .clk(and_1_out));  // open: clr
  Register #(.width(32)) register_7 (.D(INPUT_X), .en(decoder_1_out7), .Q(R7), .clk(and_1_out));  // open: clr
  Register #(.width(32)) register_8 (.D(INPUT_X), .en(decoder_1_out8), .Q(R8), .clk(and_1_out));  // open: clr
  Register #(.width(32)) register_9 (.D(INPUT_X), .en(decoder_1_out9), .Q(R9), .clk(and_1_out));  // open: clr
  Register #(.width(32)) register_10 (.D(INPUT_X), .en(decoder_1_out10), .Q(R10), .clk(and_1_out));  // open: clr
  Register #(.width(32)) register_11 (.D(INPUT_X), .en(decoder_1_out11), .Q(R11), .clk(and_1_out));  // open: clr
  Register #(.width(32)) register_12 (.D(INPUT_X), .en(decoder_1_out12), .Q(R12), .clk(and_1_out));  // open: clr
  Register #(.width(32)) register_13 (.D(INPUT_X), .en(decoder_1_out13), .Q(R13), .clk(and_1_out));  // open: clr
  Register #(.width(32)) register_14 (.D(INPUT_X), .en(decoder_1_out14), .Q(R14), .clk(and_1_out));  // open: clr
  Register #(.width(32)) register_15 (.D(INPUT_X), .en(decoder_1_out15), .Q(R15), .clk(and_1_out));  // open: clr
  Multiplexer #(.select(4), .width(32), .enable("false")) multiplexer_1 (
    .in0({32{1'b0}}), .in1(R1), .in2(R2), .in3(R3), .in4(R4), .in5(R5), .in6(R6), .in7(R7), .in8(R8),
    .in9(R9), .in10(R10), .in11(R11), .in12(R12), .in13(R13), .in14(R14), .in15(R15), .out(outY),
    .sel(inputADDRESSY));
  Multiplexer #(.select(4), .width(32), .enable("false")) multiplexer_2 (
    .in0({32{1'b0}}), .in1(R1), .in2(R2), .in3(R3), .in4(R4), .in5(R5), .in6(R6), .in7(R7), .in8(R8),
    .in9(R9), .in10(R10), .in11(R11), .in12(R12), .in13(R13), .in14(R14), .in15(R15), .out(outZ),
    .sel(inputADDRESSZ));
endmodule

module ALU (
  input  [31:0] input_a,
  input  [31:0] input_b,
  input  [3:0] in_3,
  output [31:0] out_4
);

  wire comparator_1_eq, comparator_1_lt;
  wire [4:0] bit_extender_1_out;
  wire [31:0] adder_1_out, adder_2_out, and_1_out, and_2_out, bit_extender_2_out, bit_extender_3_out,
       negator_1_out, not_1_out, or_1_out, shifter_1_out, shifter_2_out, shifter_3_out, shifter_4_out,
       xor_1_out;

  Bit_Extender #(.in_width(32), .out_width(5)) bit_extender_1 (.in(input_b), .out(bit_extender_1_out));
  assign not_1_out = ~input_a;  // NOT_Gate not_1, 32 bits wide
  Negator #(.width(32)) negator_1 (.in(input_a), .out(negator_1_out));
  assign and_1_out = input_a & input_b;  // AND_Gate and_1, 32 bits wide
  assign and_2_out = not_1_out & input_b;  // AND_Gate and_2, 32 bits wide
  assign or_1_out = input_a | input_b;  // OR_Gate or_1, 32 bits wide
  assign xor_1_out = input_a ^ input_b;  // XOR_Gate xor_1, 32 bits wide
  Adder #(.width(32)) adder_1 (.a(input_a), .b(input_b), .out(adder_1_out));  // open: cin, cout
  Adder #(.width(32)) adder_2 (.a(negator_1_out), .b(input_b), .out(adder_2_out));  // open: cin, cout
  Comparator #(.width(32)) comparator_1 (
    .a(input_a), .b(input_b), .eq(comparator_1_eq), .lt(comparator_1_lt));  // open: gt
  Shifter #(.width(32)) shifter_1 (.in(input_a), .\dist (bit_extender_1_out), .out(shifter_1_out));
  Shifter #(.width(32), .shift("lr")) shifter_2 (.in(input_a), .\dist (bit_extender_1_out), .out(shifter_2_out));
  Shifter #(.width(32), .shift("ar")) shifter_3 (.in(input_a), .\dist (bit_extender_1_out), .out(shifter_3_out));
  Shifter #(.width(32), .shift("rr")) shifter_4 (.in(input_a), .\dist (bit_extender_1_out), .out(shifter_4_out));
  assign bit_extender_2_out = {{31{1'b0}}, comparator_1_eq};  // Bit_Extender bit_extender_2
  assign bit_extender_3_out = {{31{1'b0}}, comparator_1_lt};  // Bit_Extender bit_extender_3
  Multiplexer #(.select(4), .width(32), .enable("false")) multiplexer_1 (
    .in0(and_1_out), .in1(and_2_out), .in2(or_1_out), .in3(xor_1_out), .in4(adder_1_out), .in5(adder_2_out),
    .in6(bit_extender_2_out), .in7(bit_extender_3_out), .in8(shifter_1_out), .in9(shifter_2_out),
    .in10(shifter_3_out), .in11(shifter_4_out), .out(out_4), .sel(in_3));  // open: in12, in13, in14, in15
endmodule

module dataPath (
  output [1:0] out_1,
  output [7:0] out_2,
  output [15:0] out_3,
  output [7:0] out_4,
  output [3:0] out_5,
  output [3:0] out_6,
  output [3:0] out_7,
  output [1:0] out_8,
  output out_9,
  output [31:0] out_10,
  output out_11,
  output out_12,
  output out_13,
  output [31:0] out_14,
  output out_15,
  output [1:0] out_16,
  output [3:0] out_17
);

  wire comparator_1_eq, compOP, Global_clock_out, not_1_out, Reset_pc_out, SwapRegs, XORZ;
  wire [3:0] multiplexer_3_out, multiplexer_4_out, multiplexer_5_out, RegSwapped;
  wire [15:0] bit_extender_1_out, multiplexer_1_out, shifter_1_out, shifter_2_out;
  wire [19:0] adder_1_out, bit_extender_2_out, pc, PC_3;
  wire [31:0] bit_extender_3_out, bit_extender_4_out, multiplexer_6_out, multiplexer_7_out, ram_1_data;
  wire [31:1] alu_1_out_4;

  assign bit_extender_1_out = {{8{1'b0}}, out_2};  // Bit_Extender bit_extender_1
  Shifter #(.width(16)) shifter_1 (.in({out_3[15:8], out_2}), .\dist (4'b0001), .out(shifter_1_out));
  Multiplexer #(.select(2), .width(16), .enable("false")) multiplexer_1 (
    .in0(16'h1), .in1(shifter_1_out), .in2(shifter_2_out), .out(multiplexer_1_out), .sel(out_1));  // open: in3
  Shifter #(.width(16)) shifter_2 (.in(bit_extender_1_out), .\dist (4'b0001), .out(shifter_2_out));
  assign bit_extender_2_out = {{4{multiplexer_1_out[15]}}, multiplexer_1_out};  // Bit_Extender bit_extender_2
  Clock Reset_pc (.out(Reset_pc_out));
  Adder #(.width(20)) adder_1 (.a(bit_extender_2_out), .b(pc), .out(adder_1_out));  // open: cin, cout
  Clock Global_clock (.out(Global_clock_out));
  Comparator comparator_1 (.a(out_4), .b(8'h19), .eq(comparator_1_eq));  // open: gt, lt
  not not_1 (not_1_out, comparator_1_eq);
  Register #(.width(20)) u_PC (.D(adder_1_out), .en(1'b1), .Q(pc), .clk(Global_clock_out), .clr(Reset_pc_out));
  and and_1 (SwapRegs, not_1_out, XORZ);
  Adder #(.width(20)) adder_2 (.a(pc), .b(20'h3), .out(PC_3));  // open: cin, cout
  controlUnit controlunit_1 (
    .comparitor(compOP), .opcode(out_4), .pcSelection(out_1), .AluOpcode(out_17), .WDB(out_16),
    .MemR(out_15), .MemW(out_13), .ZSelect(out_12), .RegW(out_11), .XorZ(XORZ), .RegD(out_9));
  ROM #(.addrWidth(20), .dataWidth(24)) rom_1 (.addr(pc), .data({out_4, out_3[15:8], out_2}));  // open: sel
  Multiplexer #(.width(4), .enable("false")) multiplexer_2 (
    .in0(out_3[15:12]), .in1(out_3[11:8]), .out(RegSwapped), .sel(SwapRegs));
  Multiplexer #(.width(4), .enable("false")) multiplexer_3 (
    .in0(out_3[15:12]), .in1(4'b1111), .out(multiplexer_3_out), .sel(out_9));
  Multiplexer #(.width(4), .enable("false")) multiplexer_4 (
    .in0(out_3[11:8]), .in1(out_3[15:12]), .out(multiplexer_4_out), .sel(SwapRegs));
  Multiplexer #(.width(4), .enable("false")) multiplexer_5 (
    .in0(out_2[7:4]), .in1(RegSwapped), .out(multiplexer_5_out), .sel(XORZ));
  regFile regfile_1 (
    .INPUT_X(multiplexer_7_out), .inputADDRESSY(multiplexer_4_out), .inputADDRESSZ(multiplexer_5_out),
    .INPUTaddress(multiplexer_3_out), .outY(out_10), .outZ(out_14), .CLK(Global_clock_out), .regW(out_11));
  assign bit_extender_3_out = {{24{1'b0}}, out_2};  // Bit_Extender bit_extender_3
  Multiplexer #(.width(32), .enable("false")) multiplexer_6 (
    .in0(out_14), .in1(bit_extender_3_out), .out(multiplexer_6_out), .sel(out_12));
  ALU alu_1 (.input_a(out_10), .input_b(multiplexer_6_out), .in_3(out_17), .out_4({alu_1_out_4, compOP}));
  RAM #(.addrWidth(20), .dataWidth(32), .bus("separate")) ram_1 (
    .addr({alu_1_out_4[19:1], compOP}), .din(out_14), .data(ram_1_data), .str(out_13),
    .clk(Global_clock_out), .ld(out_15));  // open: sel, clr
  Multiplexer #(.select(2), .width(32), .enable("false")) multiplexer_7 (
    .in0({alu_1_out_4, compOP}), .in1(ram_1_data), .in2(bit_extender_4_out), .out(multiplexer_7_out),
    .sel(out_16));  // open: in3
  assign bit_extender_4_out = {{12{PC_3[19]}}, PC_3};  // Bit_Extender bit_extender_4

  assign out_3[7:0] = out_2;
  assign out_5 = out_3[15:12];
  assign out_6 = out_3[11:8];
  assign out_7 = out_2[7:4];
  assign out_8 = out_1;

  // Other names for the same wires on the sheet: imm8[7:0] = out_2; imm16[15:0] = {out_3[15:8], out_2};
  //   Z[3:0] = out_2[7:4]; Y[3:0] = out_3[11:8]; X[3:0] = out_3[15:12]; OP[7:0] = out_4; ALUOP[3:0] = out_17;
  //   BusY[31:0] = out_10; BusZ[31:0] = out_14; MemR = out_15; MemW = out_13; pcSelection[1:0] = out_1; RegD = out_9;
  //   RegW = out_11; WDB[1:0] = out_16; ZSel = out_12

  // Notes on the sheet:
  //   ROM
  //   contents of rom_1 (hex, n*v repeats v):
  //   9350 c3103 c5106 c6104 142303 5*0 143502 153504 7*0 153205 166501 0 165303
  //   RAM
endmodule

module controlUnit (
  input  comparitor,
  input  [7:0] opcode,
  output [1:0] pcSelection,
  output [1:0] WDB,
  output MemR,
  output MemW,
  output ZSelect,
  output RegW,
  output XorZ,
  output RegD,
  output [3:0] AluOpcode
);

  wire and_1_out, comparator_1_gt, comparator_2_lt, not_1_out;
  wire [1:0] bit_extender_1_out, multiplexer_1_out, multiplexer_2_out, multiplexer_3_out, multiplexer_4_out,
       multiplexer_5_out;
  wire [7:0] subtractor_1_out;
  wire [9:8] rom_1_data;

  Subtractor subtractor_1 (.a(opcode), .b(8'h14), .out(subtractor_1_out));  // open: bin, bout
  Multiplexer #(.width(2), .enable("false")) multiplexer_1 (
    .in0(2'b00), .in1(2'b10), .out(multiplexer_1_out), .sel(comparitor));
  Bit_Extender #(.out_width(2)) bit_extender_1 (.in(subtractor_1_out), .out(bit_extender_1_out));
  Comparator comparator_1 (.a(opcode), .b(8'h13), .gt(comparator_1_gt));  // open: eq, lt
  Comparator comparator_2 (.a(opcode), .b(8'h18), .lt(comparator_2_lt));  // open: gt, eq
  Multiplexer #(.width(2), .enable("false")) multiplexer_2 (
    .in0(2'b10), .in1(2'b00), .out(multiplexer_2_out), .sel(comparitor));
  Multiplexer #(.select(2), .width(2), .enable("false")) multiplexer_3 (
    .in0(multiplexer_1_out), .in1(multiplexer_2_out), .in2(multiplexer_4_out), .in3(multiplexer_5_out),
    .out(multiplexer_3_out), .sel(bit_extender_1_out));
  and and_1 (and_1_out, comparator_1_gt, comparator_2_lt);
  ROM #(.dataWidth(10)) rom_1 (
    .addr(opcode), .data({rom_1_data, RegD, XorZ, RegW, ZSelect, MemW, MemR, WDB}));  // open: sel
  ROM #(.dataWidth(4)) rom_2 (.addr(opcode), .data(AluOpcode));  // open: sel
  Multiplexer #(.width(2), .enable("false")) multiplexer_4 (
    .in0(2'b00), .in1(2'b10), .out(multiplexer_4_out), .sel(comparitor));
  Multiplexer #(.width(2), .enable("false")) multiplexer_5 (
    .in0(2'b10), .in1(2'b00), .out(multiplexer_5_out), .sel(comparitor));
  not not_1 (not_1_out, and_1_out);
  Multiplexer #(.width(2), .enable("false")) multiplexer_6 (
    .in0(multiplexer_3_out), .in1(rom_1_data), .out(pcSelection), .sel(not_1_out));

  // Notes on the sheet:
  //   contents of rom_1 (hex, n*v repeats v):
  //   8*20 12*30 4*40 35 58 100 1a2
  //   contents of rom_2 (hex, n*v repeats v):
  //   0 1 2 3 4 5 6 7 0 1 2 3 4 5 6 7 8 9 a b 6 6 7 7 4 4
endmodule
